// Logisim project cpu.circ as structural Verilog: 1 circuit, main circuit cpu
module cpu (
  input  clk,
  input  [31:0] Instruction,
  input  [31:0] MemReadData,
  output [31:0] MemAddress,
  output [31:0] ProgramCounter,
  output [31:0] ra,
  output [31:0] sp,
  output [31:0] t0,
  output [31:0] t1,
  output [31:0] t2,
  output [31:0] s0,
  output [31:0] s1,
  output [31:0] a0,
  output [3:0] MemWriteMask,
  output [31:0] MemWriteData
);

  wire ASel0, BrEq, BrLt, BrUn0, BSel0, MemWEn0, PCSel0, RW0;
  wire [1:0] WBSel0;
  wire [2:0] ImmSel0;
  wire [3:0] ALUsel0;
  wire [31:0] adder_2_out, ALUResult, ALUresultStage4, bit_extender_1_out, bit_extender_2_out,
       bit_extender_3_out, DataAStage3, DataBStage3, DataBStage4, Immediate, InstStage2, multiplexer_1_out,
       multiplexer_2_out, multiplexer_3_out, multiplexer_4_out, partial_load_1_datatoreg, PCPlus4, PCStage2,
       PCStage3, PCStage4, ReadData1, ReadData2, WriteData0, WriteDataStage5;
  wire [45:0] ExInstStage3, ExInstStage4, ExInstStage5;

  // Probe on Instruction
  Adder #(.width(32)) adder_1 (.a(ProgramCounter), .b(32'h4), .out(PCPlus4));  // open: cin, cout
  Register #(.width(32)) PC (.D(multiplexer_1_out), .clk(clk), .Q(ProgramCounter));  // open: en, clr
  Multiplexer #(.width(32)) multiplexer_1 (.in0(PCPlus4), .in1(ALUResult), .out(multiplexer_1_out), .sel(PCSel0));
  Multiplexer #(.width(32)) multiplexer_2 (.in0(Instruction), .in1(32'h13), .out(multiplexer_2_out), .sel(PCSel0));
  Register #(.width(32)) instID (.D(multiplexer_2_out), .en(1'b1), .clk(clk), .Q(InstStage2));  // open: clr
  Register #(.width(32)) pcID (.D(ProgramCounter), .en(1'b1), .clk(clk), .Q(PCStage2));  // open: clr
  control_logic control_logic_1 (
    .Instruction(InstStage2), .BrEq(BrEq), .BrLt(BrLt), .PCSel(PCSel0), .RegWEn(RW0), .ImmSel(ImmSel0),
    .BrUn(BrUn0), .ASel(ASel0), .BSel(BSel0), .ALUSel(ALUsel0), .MemWEn(MemWEn0), .WBSel(WBSel0));
  regfile regfile_1 (
    .ReadIndex1(InstStage2[19:15]), .ReadIndex2(InstStage2[24:20]), .WriteIndex(InstStage2[11:7]),
    .WriteData(WriteDataStage5), .RegWEn(ExInstStage5[33]), .clk(clk), .ra(ra), .sp(sp), .t0(t0), .t1(t1),
    .t2(t2), .s0(s0), .s1(s1), .a0(a0), .ReadData1(ReadData1), .ReadData2(ReadData2));
  Register #(.width(32)) pcEX (.D(PCStage2), .en(1'b1), .clk(clk), .Q(PCStage3));  // open: clr
  Register #(.width(32)) rs1EX (.D(ReadData1), .en(1'b1), .clk(clk), .Q(DataAStage3));  // open: clr
  Register #(.width(32)) rs2EX (.D(ReadData2), .en(1'b1), .clk(clk), .Q(DataBStage3));  // open: clr
  Register #(.width(46)) register_1 (
    .D({WBSel0, MemWEn0, ALUsel0, BSel0, ASel0, ImmSel0, RW0, PCSel0, InstStage2}), .en(1'b1), .clk(clk),
    .Q(ExInstStage3));  // open: clr
  Bit_Extender #(.in_width(46), .out_width(32), .\type ("zero")) bit_extender_1 (
    .in(ExInstStage3), .out(bit_extender_1_out));
  Multiplexer #(.width(32)) multiplexer_3 (
    .in0(DataAStage3), .in1(PCStage3), .out(multiplexer_3_out), .sel(ExInstStage3[37]));
  Multiplexer #(.width(32)) multiplexer_4 (
    .in0(DataBStage3), .in1(Immediate), .out(multiplexer_4_out), .sel(ExInstStage3[38]));
  alu alu_1 (.A(multiplexer_3_out), .B(multiplexer_4_out), .ALUSel(ExInstStage3[42:39]), .ALUResult(ALUResult));
  branch_comp branch_comp_1 (.BrData1(DataAStage3), .BrData2(DataBStage3), .BrUn(BrUn0), .BrEq(BrEq), .BrLt(BrLt));
  imm_gen imm_gen_1 (.Instruction(bit_extender_1_out), .ImmSel(ExInstStage3[36:34]), .Immediate(Immediate));
  Register #(.width(32)) pcMA (.D(PCStage3), .en(1'b1), .clk(clk), .Q(PCStage4));  // open: clr
  Register #(.width(32)) register_2 (.D(ALUResult), .en(1'b1), .clk(clk), .Q(ALUresultStage4));  // open: clr
  Register #(.width(32)) register_3 (.D(DataBStage3), .en(1'b1), .clk(clk), .Q(DataBStage4));  // open: clr
  Register #(.width(46)) register_4 (.D(ExInstStage3), .en(1'b1), .clk(clk), .Q(ExInstStage4));  // open: clr
  Bit_Extender #(.in_width(46), .out_width(32), .\type ("zero")) bit_extender_2 (
    .in(ExInstStage4), .out(bit_extender_2_out));
  Bit_Extender #(.in_width(46), .out_width(32), .\type ("zero")) bit_extender_3 (
    .in(ExInstStage4), .out(bit_extender_3_out));
  Adder #(.width(32)) adder_2 (.a(PCStage4), .b(32'h4), .out(adder_2_out));  // open: cin, cout
  partial_store partial_store_1 (
    .Instruction(bit_extender_2_out), .MemAddress(ALUresultStage4), .DataFromReg(DataBStage4),
    .MemWEn(ExInstStage4[43]), .MemWriteMask(MemWriteMask), .DataToMem(MemWriteData));
  partial_load partial_load_1 (
    .Instruction(bit_extender_3_out), .MemAddress(ALUresultStage4), .DataFromMem(MemReadData),
    .DataToReg(partial_load_1_datatoreg));
  Multiplexer #(.select(2), .width(32)) multiplexer_5 (
    .in0(partial_load_1_datatoreg), .in1(ALUresultStage4), .in2(adder_2_out), .out(WriteData0),
    .sel(ExInstStage4[45:44]));  // open: in3
  Register #(.width(32)) register_5 (.D(WriteData0), .en(1'b1), .clk(clk), .Q(WriteDataStage5));  // open: clr
  Register #(.width(46)) register_6 (.D(ExInstStage4), .en(1'b1), .clk(clk), .Q(ExInstStage5));  // open: clr

  // Notes on the sheet:
  //   To IMEM
  //   IMEM (do **NOT** move this)
  //   From IMEM
  //   Inputs/Outputs for testing. Do **NOT** move these.
  //   It is OK to move the PC, RegFile, ALU, MEM, Branch Comp, Imm Gen, Partial Load, Partial Store and Control Logic to wherever is most convenient for you when constructing your CPU, and to delete this text
  //   To DMEM
  //   DMEM (do **NOT** move this)
  //   From DMEM
endmodule
